# Fritzing sketch Midterm Fritzing (saved by Fritzing 1.0.2b)
breadboards: 3

parts:
  Breadboard4 = Breadboard Split Power
  Breadboard5 = Breadboard Split Power
  A1 = Particle - Photon2
  Part2 = 12 NeoPixel Ring [part_number=1643]
  U1 = ENCODER_RGB [package=encoder_led_2]
  OLED_I2C1 = OLED 128x64 I2C Monochrome Display
  M1 = BMP280
  Part1 = NeoPixel Stick [part_number=1426]
  S1 = Pushbutton [package="[THT]"]
  S2 = Pushbutton [package="[THT]"]
  S3 = Pushbutton [package="[THT]"]

nets:
  GND: Breadboard4.pin3Z, Breadboard4.pin15Z, Breadboard4.pin17Z, Breadboard4.pin20Z, Breadboard4.pin29Z, Breadboard5.pin3Z, Breadboard5.pin28Z, A1.Pin_4, A1.Pin_30, A1.Pin_35, Part2.GND, U1.C, OLED_I2C1.GND, M1.GND, Part1.GND, S3.Pin_1, S3.Pin_2
  VDD: Breadboard4.pin4Y, Breadboard4.pin15Y, Breadboard4.pin17Y, Breadboard4.pin21Y, Breadboard4.pin29Y, Breadboard5.pin3Y, Breadboard5.pin15Y, Breadboard5.pin17Y, Breadboard5.pin29Y, A1.Pin_2, A1.Pin_31, U1.+, OLED_I2C1.VDD, M1.VIN, S1.Pin_1, S1.Pin_2, S2.Pin_1, S2.Pin_2
  N1: A1.Pin_13, U1.SW
  N2: A1.Pin_14, U1.A
  N3: A1.Pin_15, U1.B#2
  N4: A1.Pin_17, OLED_I2C1.SDA, M1.SDA
  N5: A1.Pin_18, OLED_I2C1.SCK, M1.SCL
  N6: A1.Pin_19, Part1.DATAIN
  N7: A1.Pin_20, S1.Pin_3, S1.Pin_4
  N8: A1.Pin_21, S2.Pin_3, S2.Pin_4
  N9: A1.Pin_22, S3.Pin_3, S3.Pin_4
  VDD_2: A1.Pin_26, Part2.VDD, Part1.+5V
  N10: Part2.IN, Part1.DATAOUT

custom parts:
  Breadboard Split Power: A custom 6 pin per group power supply strip where the top row (ground) is all bussed together and the bottom row (+V) is split in two groups of 12 pins. This version is modified to be a loadable part and was rescaled to be on the standard 1px = 1thou grid with the size set in inches
  Particle - Photon2: The Photon 2 is a microcontroller and Wi-Fi networking developed by particle. Features: 802.11a/b/g/n Wi-Fi, 2.4 GHz and 5 GHz Integrated PCB antenna Integrated U.FL connector for external antenna Integrated RF switch BLE 5 using same antenna as Wi-Fi Realtek RTL8721DM MCU ARM Cortex M33 CPU, 200 MHz 2048 KB (2 MB) user application maximum size 3072 KB (3 MB) of RAM available to user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
  12 NeoPixel Ring: 12 ultra bright smart LED NeoPixels are arranged in a circle with 1.5" (37mm) outer diameter. The rings are 'chainable' - connect the output pin of one to the input pin of another. Use only one microcontroller pin to control as many as you can chain together! Each LED is addressable as the driver chip is inside the LED. Each one has ~18mA constant current drive so the color will be very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
  ENCODER_RGB: SparkFun RGB rotary Encoder
  BMP280: Temperature Humidity Barometric presure Sensor, I2C
  NeoPixel Stick: Make your own little LED strip arrangement with this stick of NeoPixel LEDs. We crammed 8 of the tiny 5050 (5mm x 5mm) smart RGB LEDs onto a PCB with mounting holes and a chainable design. Use only one microcontroller pin to control as many as you can chain together! Each LED is addressable as the driver chip is inside the LED. Each one has ~18mA constant current drive so the color will be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
